// Logisim project 2 input multiplexer.circ as structural Verilog: 1 circuit, main circuit main
module main (
  input  I0,
  input  Y,
  input  I1
);

  wire and_1_out, and_2_out, not_1_out, or_1_out, undriven;

  not not_1 (not_1_out, undriven);
  and and_1 (and_1_out, I0, not_1_out);
  and and_2 (and_2_out, undriven, I1);
  or or_1 (or_1_out, and_1_out, and_2_out);

  // Notes on the sheet:
  //   S0
  //   2 INPUT MULTIPLEXER
endmodule
