// Logisim project 2 x multiplexer.circ as structural Verilog: 1 circuit, main circuit main
module main (
  input  in_1,
  input  in_2,
  input  in_3
);

  wire multiplexer_1_out, undriven;

  LED led_1 (.in(multiplexer_1_out));
  Multiplexer multiplexer_1 (.in0(in_1), .in1(in_2), .out(multiplexer_1_out), .sel(undriven));  // open: en

  // Notes on the sheet:
  //   2 x Multiplexer
endmodule
