// Logisim project 3bitcounter.circ as structural Verilog: 1 circuit, main circuit main
module main (
  input  in_1,
  output out_2,
  output out_3,
  output out_4
);

  wire and_1_out, clock_1_out;

  Clock clock_1 (.out(clock_1_out));
  T_Flip_Flop t_ff_1 (.clk(clock_1_out), .T(in_1), .Q(out_2));  // open: Qn, preset, reset, en
  T_Flip_Flop t_ff_2 (.clk(clock_1_out), .T(out_2), .Q(out_3));  // open: Qn, preset, reset, en
  and and_1 (and_1_out, out_2, out_3);
  T_Flip_Flop t_ff_3 (.clk(clock_1_out), .T(and_1_out), .Q(out_4));  // open: Qn, preset, reset, en

  // Notes on the sheet:
  //   INPUT
  //   CLOCK
  //   3 BIT COUNTER
endmodule
