// Logisim project 4 input multiplexer.circ as structural Verilog: 1 circuit, main circuit main
module main (
  input  S0,
  input  S1,
  output Y
);

  wire and_1_out, and_2_out, and_3_out, and_4_out, not_1_out, not_2_out, undriven;

  not not_1 (not_1_out, S0);
  not not_2 (not_2_out, S1);
  and and_1 (and_1_out, not_1_out, not_2_out, undriven);
  and and_2 (and_2_out, not_1_out, S1, undriven);
  and and_3 (and_3_out, S0, not_2_out, undriven);
  and and_4 (and_4_out, S0, S1, undriven);
  or or_1 (Y, and_1_out, and_2_out, and_3_out, and_4_out);

  // Notes on the sheet:
  //   S0'
  //   S1'
  //   INPUT SELECTOR LINE
  //   I0
  //   I1
  //   I2
  //   I3
  //   4 INPUT MULTIPLEXER
endmodule
