// Logisim project 8 input multiplexer.circ as structural Verilog: 1 circuit, main circuit main
module main (
  input  S0,
  input  S1,
  input  S2,
  output Y
);

  wire and_1_out, and_2_out, and_3_out, and_4_out, and_5_out, and_6_out, and_7_out, and_8_out, not_1_out,
       not_2_out, not_3_out, undriven;

  not not_1 (not_1_out, S0);
  not not_2 (not_2_out, S1);
  not not_3 (not_3_out, S2);
  and and_1 (and_1_out, not_1_out, not_2_out, not_3_out, undriven);
  and and_2 (and_2_out, not_1_out, not_2_out, S2, undriven);
  and and_3 (and_3_out, not_1_out, S1, not_3_out, undriven);
  and and_4 (and_4_out, not_1_out, S1, S2, undriven);
  and and_5 (and_5_out, S0, not_2_out, not_3_out, undriven);
  and and_6 (and_6_out, S0, not_2_out, S2, undriven);
  and and_7 (and_7_out, S0, S1, not_3_out, undriven);
  and and_8 (and_8_out, S0, S1, S2, undriven);
  or or_1 (Y, and_1_out, and_2_out, and_3_out, and_4_out, and_5_out, and_6_out, and_7_out, and_8_out);

  // Notes on the sheet:
  //   S0'
  //   S1'
  //   S2'
  //   8 INPUT MULTIPLEXER
  //   I0
  //   I1
  //   I2
  //   I3
  //   I4
  //   I5
  //   I6
  //   I7
endmodule
