// Logisim project 8x1multiplexer.circ as structural Verilog: 1 circuit, main circuit main
module main (
  input  in_1,
  input  in_2,
  input  in_3,
  input  in_4,
  input  in_5,
  input  in_6,
  input  in_7,
  input  in_8,
  input  [2:0] in_9
);

  wire multiplexer_1_out;
  wire [2:0] undriven;

  Multiplexer #(.select(3)) multiplexer_1 (
    .in0(in_1), .in1(in_2), .in2(in_3), .in3(in_4), .in4(in_5), .in5(in_6), .in6(in_7), .in7(in_8),
    .out(multiplexer_1_out), .sel(undriven));  // open: en
  LED led_1 (.in(multiplexer_1_out));

  // Notes on the sheet:
  //   8 x 1 Multiplexer
endmodule
