// Logisim project Class-1.circ as structural Verilog: 1 circuit, main circuit main
module main (
  input  A,
  input  A_2,
  input  A_3,
  input  B,
  input  B_2,
  input  A_4,
  input  A_5,
  input  A_6,
  input  in_9,
  input  in_10,
  input  A_7,
  input  A_8,
  input  in_13,
  input  in_14,
  output B_3,
  output C,
  output B_4,
  output B_5,
  output out_19,
  output out_20,
  output out_21,
  output out_22
);

  buf buffer_1 (B_5, A_6);
  and and_1 (C, A_2, B);
  xor xor_1 (out_22, A_8, in_14);
  or or_1 (B_4, A, B_2);
  nand nand_1 (out_19, A_4, in_9);
  Controlled_Inverter controlled_inverter_1 (.in(A_3), .out(B_3));  // open: en
  xnor xnor_1 (out_21, A_7, in_13);
  nor nor_1 (out_20, A_5, in_10);

  // Notes on the sheet:
  //   1) AND GATE
  //   4) Buffer
  //   7) EXCLUSIVE OR (XOR)
  //   2) OR GATE
  //   5) NAND GATE
  //   3) Inverter
  //   6) NOR GATE
  //   8) EXCLUSIVE NOR (XNOR)
endmodule
