// Logisim project Class-2.circ as structural Verilog: 1 circuit, main circuit main
module main (
  input  A,
  input  B,
  input  A_2,
  input  B_2,
  output out_5,
  output out_6
);

  wire A_prime_B_out, AB_out, not_1_out;

  not not_1 (not_1_out, A_2);
  and AB (AB_out, A, B);
  and A_prime_B (A_prime_B_out, not_1_out, B_2);
  or A_AB (out_5, AB_out, A);
  or A_A_prime_B (out_6, A_prime_B_out, A_2);

  // Notes on the sheet:
  //   1) A+AB=A
  //   2) A+A'B=A+B
  //   A'
endmodule
