// Logisim project c3.1.circ as structural Verilog: 1 circuit, main circuit main
module main (
  input  x,
  input  y,
  output Sum,
  output Carry
);

  wire not_1_out, not_2_out, x_prime_y_out, xy_prime_out;

  not not_1 (not_1_out, x);
  not not_2 (not_2_out, y);
  and xy (Carry, x, y);
  and x_prime_y (x_prime_y_out, not_1_out, y);
  and xy_prime (xy_prime_out, x, not_2_out);
  or x_prime_y_prime (Sum, x_prime_y_out, xy_prime_out);

  // Notes on the sheet:
  //   x'
endmodule
