// Logisim project decoder.circ as structural Verilog: 1 circuit, main circuit main
module main (
  input  A,
  input  B,
  input  E,
  output D0,
  output D1,
  output D2,
  output D3
);

  wire not_1_out, not_2_out;

  not not_1 (not_1_out, A);
  not not_2 (not_2_out, B);
  and a_prime_b_prime (D0, not_2_out, E, not_1_out);
  and a_prime_b (D1, B, not_1_out, E);
  and ab_prime (D2, not_2_out, not_1_out, E);
  and ab (D3, A, B, E);

  // Notes on the sheet:
  //   Design and Simulate the Decoder 2 X 4
endmodule
