// Logisim project decoder3x8.circ as structural Verilog: 1 circuit, main circuit main
module main (
  input  X,
  input  Y,
  input  Z,
  input  E,
  output X_prime_Y_prime_Z_prime,
  output X_prime_Y_prime_Z,
  output X_prime_YZ_prime,
  output X_prime_YZ,
  output XY_prime_Z_prime,
  output XY_prime_Z,
  output XYZ_prime,
  output XYZ
);

  wire not_1_out, not_2_out, not_3_out;

  not not_1 (not_1_out, X);
  not not_2 (not_2_out, Y);
  not not_3 (not_3_out, Z);
  and D0 (X_prime_Y_prime_Z_prime, not_1_out, not_2_out, not_3_out);
  and D1 (X_prime_Y_prime_Z, not_1_out, not_2_out, Z);
  and D2 (X_prime_YZ_prime, not_1_out, Y, not_3_out);
  and D3 (X_prime_YZ, not_1_out, Y, Z);
  and D4 (XY_prime_Z_prime, X, not_2_out, not_3_out);
  and D5 (XY_prime_Z, X, not_2_out, Z);
  and D6 (XYZ_prime, X, Y, not_3_out);
  and D7 (XYZ, X, Y, Z);

  // Notes on the sheet:
  //   Design and Simulate the Decoder 3 X 8
endmodule
