// Logisim project full adder.circ as structural Verilog: 1 circuit, main circuit main
module main (
  input  X,
  input  Y,
  input  Z,
  output Sum,
  output Carry
);

  wire and_1_out, xor_1_out, yz_out;

  xor xor_1 (xor_1_out, X, Y);
  and yz (yz_out, X, Y);
  and and_1 (and_1_out, Z, xor_1_out);
  xor xor_2 (Sum, xor_1_out, Z);
  or or_1 (Carry, yz_out, and_1_out);

  // Notes on the sheet:
  //   Full Adder
  //   y+z
  //   x(y+z)
  //   x + y + z
  //   yz + x(y+z)
endmodule
