// Logisim project half adder.circ as structural Verilog: 1 circuit, main circuit main
module main (
  input  X,
  input  Y,
  output X___Y,
  output XY
);

  xor xor_1 (X___Y, X, Y);
  and u_XY (XY, X, Y);

  // Notes on the sheet:
  //   Half Ladder
  //   xory
endmodule
