// Logisim project inputmultiplier.circ as structural Verilog: 1 circuit, main circuit main
module main (
  input  So,
  input  S1,
  output out_3,
  output out_4,
  output out_5,
  output out_6
);

  wire not_1_out, not_2_out, undriven, undriven_2;

  not not_1 (not_1_out, undriven);
  not not_2 (not_2_out, undriven_2);
  and and_1 (out_3, undriven, not_1_out, not_2_out);
  and and_2 (out_4, not_1_out, undriven_2, undriven);
  and and_3 (out_5, undriven, not_2_out, undriven);
  and and_4 (out_6, undriven, undriven_2, undriven);

  // Notes on the sheet:
  //   Io
  //   I1
  //   I2
  //   I3
  //   So'
  //   S1'
  //   4 - Input Multiplier
  //   So'S1'Io
  //   So'S1I1
  //   SoS1'I2
  //   SoS1I3
endmodule
